# Fritzing sketch dfplayer (saved by Fritzing 0.9.3b)
breadboards: 1

parts:
  DFRobot_DFPlayer_Mini1 = DFRobot DFPlayer Mini [part_number=DFR0299]
  R1 = Resistor [tolerance=±5% resistance=1k package="0402 [SMD]"]
  C1 = Capacitor Polarized [package=panasonic_g]
  SPKR1 = Loudspeaker
  HLK-PM1 = HLK-PM01
  Parça1 = Bluetooth HC-05 Macho
  R3 = Resistor [tolerance=±5% resistance=1k part_number="3.3V için kullanıldı." package="0402 [SMD]"]
  R4 = Resistor [tolerance=±5% resistance=2k part_number="3.3V için kullanıldı" package="0402 [SMD]"]
  R2 = Resistor [tolerance=±5% resistance=1k package="0402 [SMD]"]
  U1 = Mono 2.6W Class D Amplifier [package=8-tdfn-ep]
  SPKR2 = Loudspeaker

nets:
  VCC: DFRobot_DFPlayer_Mini1.VCC, HLK-PM1.+Vo, Parça1.VCC
  N1: DFRobot_DFPlayer_Mini1.RX, R1.Pin_1
  N2: DFRobot_DFPlayer_Mini1.TX, R2.Pin_1
  N3: DFRobot_DFPlayer_Mini1.DAC_R, U1.IN+
  N4: DFRobot_DFPlayer_Mini1.GND-1, DFRobot_DFPlayer_Mini1.GND-2, SPKR1.pin1, HLK-PM1.-Vo, Parça1.GND, R4.Pin_0, U1.IN-
  N5: DFRobot_DFPlayer_Mini1.SPK_2, C1.+
  N6: R1.Pin_0, Parça1.RXD
  N7: C1.-, SPKR1.pin2
  N8: Parça1.TXD, R3.Pin_0, R4.Pin_1
  N9: R3.Pin_1, R2.Pin_0
  N10: U1.OUT-, SPKR2.pin1
  N11: U1.OUT+, SPKR2.pin2

notes:
  DAC IN+
  mono amp.
  ister spk çıkışını kullanın. İsterseniz DAC çıkışına amfi bağlayın.
