# Fritzing sketch arduino_esp01 (saved by Fritzing 0.9.3b)
breadboards: 1

parts:
  Arduino_nano_168 = Arduino Nano (Rev3.0)
  R1 = Resistor [tolerance=±5% resistance=2.2k package=THT]
  LED1 = LED - 5mm [color="Red (633nm)" package="5 mm [THT]"]
  R2 = Resistor [tolerance=±5% resistance=3.3k package=THT]
  R4 = Resistor [tolerance=±5% resistance=10k package=THT]
  U2 = Voltage Regulator - 3.3V [package="TO220 [THT]"]
  R5 = Resistor [tolerance=±5% resistance=330 package=THT]
  LED2 = LED - 5mm [color="Red (633nm)" package="5 mm [THT]"]
  R6 = Resistor [tolerance=±5% resistance=330 package=THT]
  ESP-01 = ESP8266 WiFi Module [part_number=ESP8266]
  R9 = Resistor [tolerance=±5% resistance=10k package=THT]
  R10 = Resistor [tolerance=±5% resistance=10k package=THT]
  S1 = Pushbutton [package=THT]
  S3 = Toggle Switch [package=THT]
  R11 = Resistor [tolerance=±5% resistance=10k package=THT]

nets:
  N1: Arduino_nano_168.D1/TX, R1.Pin_1
  N2: Arduino_nano_168.D0/RX, ESP-01.TXD
  GND: Arduino_nano_168.GND, LED1.cathode, R2.Pin_0, U2.GND, LED2.cathode, ESP-01.GND, S1.leg1, S3.L1
  N3: Arduino_nano_168.D11/MOSI, R5.Pin_0
  N4: Arduino_nano_168.D12/MISO, R6.Pin_0
  N5: Arduino_nano_168.5V, U2.input_voltage
  N6: R1.Pin_0, R2.Pin_1, ESP-01.RXD
  N7: LED1.anode, R5.Pin_1
  N8: R4.Pin_0, U2.output_voltage, ESP-01.VCC, R9.Pin_0, R10.Pin_0, R11.Pin_0
  N9: R4.Pin_1, ESP-01.CH_PD
  N10: LED2.anode, R6.Pin_1
  N11: ESP-01.GPIO_0, R9.Pin_1, S3.COM
  N12: ESP-01.RST, S1.leg0, R11.Pin_1
  N13: ESP-01.GPIO_2, R10.Pin_1

notes:
  [deneme kısmı]
  10K 4 adet PULLUP direnci 3V3 e bağlı olmalı.
  ESP8266-01 KULLANIM VE PROGRAMLAMA ŞEMASI
  www.mikrobotik.com

custom parts:
  ESP8266 WiFi Module: Generic WiFi Module based on the ESP8266 with onboard PCB antenna and UART communications
