# Fritzing sketch tea5767 (saved by Fritzing 0.9.4)
breadboards: 1

parts:
  M1 = TEA5767 [package=THT]
  Parça1 = Arduino Uno (Rev3)
  IR1 = TSOP312.., 314.. [package=THT]
  Parça2 = DeuLigne 1.1 - The Snootlab's LCD shield for Arduino

nets:
  5V: M1.pin1, Parça1.5V, IR1.Vs, Parça2.+5V
  N1: M1.pin2, Parça1.A4/SDA, Parça2.A4(SDA)
  N2: M1.pin3, Parça1.A5/SCL, Parça2.A5(CLK)
  GND: M1.pin4, Parça1.GND, IR1.GND, Parça2.GND
  N3: Parça1.D11_PWM/MOSI, IR1.Data

notes:
  I2C LCD
  A4= SDA , A5=SCL
  TEA5767 MODÜL

custom parts:
  TEA5767: SMAKN brand new 76-108MHZ 5V TEA5767 FM Stereo Radio Module with Cable Antenna for Arduino EK1705(New version)
